# Fritzing sketch Aquaduino Sketch (saved by Fritzing 0.9.2b)
breadboards: 1

parts:
  Pro_Micro1 = Pro Micro  # not connected
  T1 = LM35 Temperature Sensor [package="TO92 [THT]"]
  U1 = Voltage Regulator - 5V [package="TO220 [THT]"]
  U2 = Voltage Regulator - 5V [package="TO220 [THT]"]
  U3 = Voltage Regulator - 5V [package="TO220 [THT]"]
  LED1 = LED - 5mm [color="Red (633nm)" package="5 mm [THT]"]
  R1 = Resistor [tolerance=±5% resistance=220 package=THT]
  MIC1 = Microphone
  7SEG1 = 7-Segment LED I2C Backpack (blue)  # not connected

nets:
  N1: T1.+Vs, U1.input_voltage, U2.input_voltage, U3.input_voltage, R1.Pin_1
  N2: T1.Vout, R1.Pin_0
  N3: T1.GND, U1.output_voltage, U2.output_voltage, U3.output_voltage, LED1.anode, MIC1.pin1

custom parts:
  Pro Micro: The SparkFun Pro Micro is a complete USB-based microcontoller development system, in a very small footprint, capable of implementing many types of projects. All programming can be done via the USB port.
  7-Segment LED I2C Backpack (blue): 4-digit, 7-segment LED Display with I2C Control
